// Logisim project riscv_simulator.circ as structural Verilog: 1 circuit, main circuit main
module main (
  input  in_1,
  input  in_2,
  input  in_3,
  input  in_4,
  input  in_5,
  input  in_6,
  input  in_7,
  input  in_8,
  input  in_9,
  input  in_10,
  input  in_11,
  input  in_12,
  input  in_13,
  input  in_14,
  input  in_15,
  output [31:0] out_16,
  output [31:0] out_17,
  output [6:0] out_18,
  output [31:0] out_19,
  output [31:0] out_20,
  output [31:0] out_21,
  output [3:0] out_22
);

  wire and_1_out, and_2_out, clock_1_out, clock_2_out, clock_4_out, clock_5_out, clock_6_out, clock_7_out,
       clock_8_out, comparator_1_eq, comparator_2_eq, comparator_3_eq, comparator_4_eq, comparator_5_eq,
       comparator_6_eq, comparator_7_eq, comparator_8_eq, comparator_9_eq, not_1_out, not_3_out, or_1_out,
       or_2_out, or_3_out, PC_INC;
  wire [2:0] priority_encoder_1_out;
  wire [5:0] register_1_q, State, undriven;
  wire [7:0] decoder_2_out0, decoder_2_out8, decoder_2_out16, decoder_2_out24, decoder_3_out0,
       decoder_3_out8, decoder_3_out16, decoder_3_out24;
  wire [15:0] MDR_q, MDR_q_2, ram_1_dout, ram_2_dout;
  wire [30:0] multiplexer_9_out;
  wire [31:0] adder_1_out, adder_2_out, adder_3_out, and_3_out, bit_extender_1_out, bit_extender_2_out,
       bit_extender_3_out, bit_extender_4_out, bit_extender_5_out, controlled_buffer_1_out,
       controlled_buffer_3_out, controlled_buffer_4_out, controlled_buffer_19_out, controlled_buffer_69_out,
       MAR_q, Microinstr, multiplexer_1_out, multiplexer_2_out, multiplexer_3_out, multiplexer_5_out,
       multiplexer_6_out, multiplexer_7_out, multiplexer_8_out, multiplexer_10_out, not_2_out, or_4_out,
       x1_q, x2_q, x3_q, x4_q, x5_q, x6_q, x7_q, x8_q, x9_q, x10_q, x11_q, x12_q, x13_q, x14_q, x15_q, x16_q,
       x17_q, x18_q, x19_q, x20_q, x21_q, x22_q, x23_q, x24_q, x25_q, x26_q, x27_q, x28_q, x29_q, x30_q,
       x31_q, xor_1_out, xor_2_out;
  wire [31:1] decoder_1_out1;
  wire [63:0] rom_1_data;

  Comparator #(.width(7)) comparator_1 (.a(out_17[6:0]), .b(7'b0110011), .eq(comparator_1_eq));  // open: gt, lt
  Comparator #(.width(7)) comparator_2 (.a(out_17[6:0]), .b(7'b0010011), .eq(comparator_2_eq));  // open: gt, lt
  Comparator #(.width(7)) comparator_3 (.a(out_17[6:0]), .b(7'b0000011), .eq(comparator_3_eq));  // open: gt, lt
  Comparator #(.width(7)) comparator_4 (.a(out_17[6:0]), .b(7'b1100111), .eq(comparator_4_eq));  // open: gt, lt
  Comparator #(.width(7)) comparator_5 (.a(out_17[6:0]), .b(7'b0100011), .eq(comparator_5_eq));  // open: gt, lt
  Comparator #(.width(7)) comparator_6 (.a(out_17[6:0]), .b(7'b1100011), .eq(comparator_6_eq));  // open: gt, lt
  Comparator #(.width(7)) comparator_7 (.a(out_17[6:0]), .b(7'b0110111), .eq(comparator_7_eq));  // open: gt, lt
  Comparator #(.width(7)) comparator_8 (.a(out_17[6:0]), .b(7'b0010111), .eq(comparator_8_eq));  // open: gt, lt
  Comparator #(.width(7)) comparator_9 (.a(out_17[6:0]), .b(7'b1101111), .eq(comparator_9_eq));  // open: gt, lt
  or or_1 (or_1_out, comparator_2_eq, comparator_3_eq, comparator_4_eq);
  or or_2 (or_2_out, comparator_7_eq, comparator_8_eq);
  Priority_Encoder priority_encoder_1 (
    .in0(comparator_1_eq), .in1(or_1_out), .in2(comparator_5_eq), .in3(comparator_6_eq), .in4(or_2_out),
    .in5(comparator_9_eq), .out(priority_encoder_1_out));  // open: in6, in7, en_in, gs, en_out
  Register #(.width(32)) IR (.D(controlled_buffer_19_out), .en(in_5), .clk(clock_1_out), .Q(out_17), .clr(in_1));
  Clock clock_1 (.out(clock_1_out));
  Clock clock_2 (.out(clock_2_out));
  assign controlled_buffer_1_out = in_7 ? out_17 : 32'bz;  // Controlled_Buffer controlled_buffer_1
  Register #(.width(32)) MAR (.D(controlled_buffer_19_out), .en(in_11), .clk(clock_2_out), .Q(MAR_q), .clr(in_1));
  and and_1 (and_1_out, in_14, in_15);
  RAM #(.addrWidth(16), .dataWidth(16)) ram_1 (
    .addr(MAR_q[31:16]), .we(and_1_out), .oe(and_2_out), .clk(clock_2_out), .din(MDR_q_2), .dout(ram_1_dout));
  and and_2 (and_2_out, in_15, ~in_14);  // AND_Gate
  Clock clock_3 ();  // open: out
  Adder #(.width(32)) adder_1 (.a(out_19), .b(controlled_buffer_3_out), .out(adder_1_out));  // open: cin, cout
  not not_1 (not_1_out, in_1);
  Multiplexer #(.width(32)) multiplexer_1 (
    .in0({32{1'b0}}), .in1(multiplexer_2_out), .out(multiplexer_1_out), .sel(not_1_out));
  or or_3 (or_3_out, in_1, in_4);
  Clock clock_4 (.out(clock_4_out));
  Multiplexer #(.width(32)) multiplexer_2 (.in0(adder_2_out), .in1(adder_1_out), .out(multiplexer_2_out), .sel(in_2));
  Multiplexer #(.width(32)) multiplexer_3 (.in0(32'h4), .in1(out_19), .out(multiplexer_3_out), .sel(PC_INC));
  Register #(.width(32)) PC (.D(multiplexer_1_out), .en(or_3_out), .clk(clock_4_out), .Q(out_16));  // open: clr
  Adder #(.width(32)) adder_2 (.a(multiplexer_3_out), .b(out_16), .out(adder_2_out));  // open: cin, cout
  assign bit_extender_1_out = {{20{out_17[31]}}, out_17[31:20]};  // Bit_Extender bit_extender_1
  assign bit_extender_2_out = {{20{out_17[31]}}, {out_17[31:25], out_17[11:7]}};  // Bit_Extender bit_extender_2
  assign controlled_buffer_1_out = in_3 ? out_16 : 32'bz;  // Controlled_Buffer controlled_buffer_2
  assign bit_extender_3_out = {{19{out_17[31]}}, {out_17[31], out_17[7], out_17[30:25], out_17[11:8], 1'b0}};  // Bit_Extender bit_extender_3
  assign bit_extender_4_out = {{11{out_17[31]}}, {out_17[31], out_17[19:12], out_17[20], out_17[30:21], 1'b0}};  // Bit_Extender bit_extender_4
  RAM #(.addrWidth(16), .dataWidth(16)) ram_2 (
    .addr(MAR_q[15:0]), .we(and_1_out), .oe(and_2_out), .clk(clock_2_out), .din(MDR_q), .dout(ram_2_dout));
  Multiplexer #(.select(3), .width(32)) multiplexer_4 (
    .in1(bit_extender_1_out), .in2(bit_extender_2_out), .in3(bit_extender_3_out),
    .in4({out_17[31:12], {12{1'b0}}}), .in5(bit_extender_4_out), .out(out_19));  // open: in0, in6, in7, sel
  Decoder #(.select(5)) decoder_1 (
    .out1(decoder_1_out1[1]), .out2(decoder_1_out1[2]), .out3(decoder_1_out1[3]), .out4(decoder_1_out1[4]),
    .out5(decoder_1_out1[5]), .out6(decoder_1_out1[6]), .out7(decoder_1_out1[7]), .out8(decoder_1_out1[8]),
    .out9(decoder_1_out1[9]), .out10(decoder_1_out1[10]), .out11(decoder_1_out1[11]),
    .out12(decoder_1_out1[12]), .out13(decoder_1_out1[13]), .out14(decoder_1_out1[14]),
    .out15(decoder_1_out1[15]), .out16(decoder_1_out1[16]), .out17(decoder_1_out1[17]),
    .out18(decoder_1_out1[18]), .out19(decoder_1_out1[19]), .out20(decoder_1_out1[20]),
    .out21(decoder_1_out1[21]), .out22(decoder_1_out1[22]), .out23(decoder_1_out1[23]),
    .out24(decoder_1_out1[24]), .out25(decoder_1_out1[25]), .out26(decoder_1_out1[26]),
    .out27(decoder_1_out1[27]), .out28(decoder_1_out1[28]), .out29(decoder_1_out1[29]),
    .out30(decoder_1_out1[30]), .out31(decoder_1_out1[31]), .sel(out_17[11:7]), .en(in_6));  // open: out0
  Clock clock_5 (.out(clock_5_out));
  Register #(.width(32)) x1 (
    .D(controlled_buffer_1_out), .en(decoder_1_out1[1]), .clk(clock_5_out), .Q(x1_q));  // open: clr
  Register #(.width(32)) x2 (
    .D(controlled_buffer_1_out), .en(decoder_1_out1[2]), .clk(clock_5_out), .Q(x2_q));  // open: clr
  Register #(.width(32)) x3 (
    .D(controlled_buffer_1_out), .en(decoder_1_out1[3]), .clk(clock_5_out), .Q(x3_q));  // open: clr
  Register #(.width(32)) x4 (
    .D(controlled_buffer_1_out), .en(decoder_1_out1[4]), .clk(clock_5_out), .Q(x4_q));  // open: clr
  Register #(.width(32)) x5 (
    .D(controlled_buffer_1_out), .en(decoder_1_out1[5]), .clk(clock_5_out), .Q(x5_q));  // open: clr
  Register #(.width(32)) x6 (
    .D(controlled_buffer_1_out), .en(decoder_1_out1[6]), .clk(clock_5_out), .Q(x6_q));  // open: clr
  Register #(.width(32)) x7 (
    .D(controlled_buffer_1_out), .en(decoder_1_out1[7]), .clk(clock_5_out), .Q(x7_q));  // open: clr
  Multiplexer #(.width(32)) multiplexer_5 (
    .in0(controlled_buffer_19_out), .in1(multiplexer_6_out), .out(multiplexer_5_out), .sel(in_13));
  Multiplexer #(.select(2), .width(32)) multiplexer_6 (
    .in0({32{1'b0}}), .in1({32{1'b0}}), .in2({32{1'b0}}), .in3({ram_1_dout, ram_2_dout}),
    .out(multiplexer_6_out));  // open: sel
  // Probe on {ram_1_dout, ram_2_dout}
  Register #(.width(32)) MDR (.D(multiplexer_5_out), .en(in_12), .clk(clock_6_out), .Q({MDR_q_2, MDR_q}), .clr(in_1));
  Clock clock_6 (.out(clock_6_out));
  assign controlled_buffer_3_out = decoder_2_out0[0] ? {32{1'b0}} : 32'bz;  // Controlled_Buffer controlled_buffer_3
  assign controlled_buffer_4_out = decoder_3_out0[0] ? {32{1'b0}} : 32'bz;  // Controlled_Buffer controlled_buffer_4
  assign controlled_buffer_3_out = decoder_2_out0[1] ? x1_q : 32'bz;  // Controlled_Buffer controlled_buffer_5
  assign controlled_buffer_4_out = decoder_3_out0[1] ? x1_q : 32'bz;  // Controlled_Buffer controlled_buffer_6
  assign controlled_buffer_3_out = decoder_2_out0[2] ? x2_q : 32'bz;  // Controlled_Buffer controlled_buffer_7
  assign controlled_buffer_4_out = decoder_3_out0[2] ? x2_q : 32'bz;  // Controlled_Buffer controlled_buffer_8
  assign controlled_buffer_3_out = decoder_2_out0[3] ? x3_q : 32'bz;  // Controlled_Buffer controlled_buffer_9
  assign controlled_buffer_4_out = decoder_3_out0[3] ? x3_q : 32'bz;  // Controlled_Buffer controlled_buffer_10
  assign controlled_buffer_3_out = decoder_2_out0[4] ? x4_q : 32'bz;  // Controlled_Buffer controlled_buffer_11
  assign controlled_buffer_4_out = decoder_3_out0[4] ? x4_q : 32'bz;  // Controlled_Buffer controlled_buffer_12
  assign controlled_buffer_3_out = decoder_2_out0[5] ? x5_q : 32'bz;  // Controlled_Buffer controlled_buffer_13
  assign controlled_buffer_4_out = decoder_3_out0[5] ? x5_q : 32'bz;  // Controlled_Buffer controlled_buffer_14
  assign controlled_buffer_3_out = decoder_2_out0[6] ? x6_q : 32'bz;  // Controlled_Buffer controlled_buffer_15
  assign controlled_buffer_4_out = decoder_3_out0[6] ? x6_q : 32'bz;  // Controlled_Buffer controlled_buffer_16
  assign controlled_buffer_3_out = decoder_2_out0[7] ? x7_q : 32'bz;  // Controlled_Buffer controlled_buffer_17
  assign controlled_buffer_4_out = decoder_3_out0[7] ? x7_q : 32'bz;  // Controlled_Buffer controlled_buffer_18
  Register #(.width(32)) x8 (
    .D(controlled_buffer_1_out), .en(decoder_1_out1[8]), .clk(clock_5_out), .Q(x8_q));  // open: clr
  Register #(.width(32)) x9 (
    .D(controlled_buffer_1_out), .en(decoder_1_out1[9]), .clk(clock_5_out), .Q(x9_q));  // open: clr
  Register #(.width(32)) x10 (
    .D(controlled_buffer_1_out), .en(decoder_1_out1[10]), .clk(clock_5_out), .Q(x10_q));  // open: clr
  Register #(.width(32)) x11 (
    .D(controlled_buffer_1_out), .en(decoder_1_out1[11]), .clk(clock_5_out), .Q(x11_q));  // open: clr
  Register #(.width(32)) x12 (
    .D(controlled_buffer_1_out), .en(decoder_1_out1[12]), .clk(clock_5_out), .Q(x12_q));  // open: clr
  Register #(.width(32)) x13 (
    .D(controlled_buffer_1_out), .en(decoder_1_out1[13]), .clk(clock_5_out), .Q(x13_q));  // open: clr
  Register #(.width(32)) x14 (
    .D(controlled_buffer_1_out), .en(decoder_1_out1[14]), .clk(clock_5_out), .Q(x14_q));  // open: clr
  Register #(.width(32)) x15 (
    .D(controlled_buffer_1_out), .en(decoder_1_out1[15]), .clk(clock_5_out), .Q(x15_q));  // open: clr
  assign controlled_buffer_19_out = in_8 ? {MDR_q_2, MDR_q} : 32'bz;  // Controlled_Buffer controlled_buffer_19
  assign controlled_buffer_3_out = decoder_2_out8[0] ? x8_q : 32'bz;  // Controlled_Buffer controlled_buffer_20
  assign controlled_buffer_3_out = decoder_2_out8[1] ? x9_q : 32'bz;  // Controlled_Buffer controlled_buffer_21
  assign controlled_buffer_3_out = decoder_2_out8[2] ? x10_q : 32'bz;  // Controlled_Buffer controlled_buffer_22
  assign controlled_buffer_3_out = decoder_2_out8[3] ? x11_q : 32'bz;  // Controlled_Buffer controlled_buffer_23
  assign controlled_buffer_3_out = decoder_2_out8[4] ? x12_q : 32'bz;  // Controlled_Buffer controlled_buffer_24
  assign controlled_buffer_3_out = decoder_2_out8[5] ? x13_q : 32'bz;  // Controlled_Buffer controlled_buffer_25
  assign controlled_buffer_3_out = decoder_2_out8[6] ? x14_q : 32'bz;  // Controlled_Buffer controlled_buffer_26
  assign controlled_buffer_3_out = decoder_2_out8[7] ? x15_q : 32'bz;  // Controlled_Buffer controlled_buffer_27
  Register #(.width(32)) x16 (
    .D(controlled_buffer_1_out), .en(decoder_1_out1[16]), .clk(clock_5_out), .Q(x16_q));  // open: clr
  assign controlled_buffer_4_out = decoder_3_out8[0] ? x8_q : 32'bz;  // Controlled_Buffer controlled_buffer_28
  Register #(.width(32)) x17 (
    .D(controlled_buffer_1_out), .en(decoder_1_out1[17]), .clk(clock_5_out), .Q(x17_q));  // open: clr
  assign controlled_buffer_4_out = decoder_3_out8[1] ? x9_q : 32'bz;  // Controlled_Buffer controlled_buffer_29
  Register #(.width(32)) x18 (
    .D(controlled_buffer_1_out), .en(decoder_1_out1[18]), .clk(clock_5_out), .Q(x18_q));  // open: clr
  assign controlled_buffer_4_out = decoder_3_out8[2] ? x10_q : 32'bz;  // Controlled_Buffer controlled_buffer_30
  Register #(.width(32)) x19 (
    .D(controlled_buffer_1_out), .en(decoder_1_out1[19]), .clk(clock_5_out), .Q(x19_q));  // open: clr
  assign controlled_buffer_4_out = decoder_3_out8[3] ? x11_q : 32'bz;  // Controlled_Buffer controlled_buffer_31
  Register #(.width(32)) x20 (
    .D(controlled_buffer_1_out), .en(decoder_1_out1[20]), .clk(clock_5_out), .Q(x20_q));  // open: clr
  assign controlled_buffer_4_out = decoder_3_out8[4] ? x12_q : 32'bz;  // Controlled_Buffer controlled_buffer_32
  Register #(.width(32)) x21 (
    .D(controlled_buffer_1_out), .en(decoder_1_out1[21]), .clk(clock_5_out), .Q(x21_q));  // open: clr
  assign controlled_buffer_4_out = decoder_3_out8[5] ? x13_q : 32'bz;  // Controlled_Buffer controlled_buffer_33
  Register #(.width(32)) x22 (
    .D(controlled_buffer_1_out), .en(decoder_1_out1[22]), .clk(clock_5_out), .Q(x22_q));  // open: clr
  assign controlled_buffer_4_out = decoder_3_out8[6] ? x14_q : 32'bz;  // Controlled_Buffer controlled_buffer_34
  Register #(.width(32)) x23 (
    .D(controlled_buffer_1_out), .en(decoder_1_out1[23]), .clk(clock_5_out), .Q(x23_q));  // open: clr
  assign controlled_buffer_4_out = decoder_3_out8[7] ? x15_q : 32'bz;  // Controlled_Buffer controlled_buffer_35
  assign bit_extender_5_out = {{31{1'b0}}, 1'b0};  // Bit_Extender bit_extender_5
  assign and_3_out = controlled_buffer_4_out & multiplexer_10_out;  // AND_Gate and_3, 32 bits wide
  assign or_4_out = controlled_buffer_4_out | multiplexer_10_out;  // OR_Gate or_4, 32 bits wide
  assign xor_1_out = controlled_buffer_4_out ^ multiplexer_10_out;  // XOR_Gate xor_1, 32 bits wide
  assign not_2_out = ~multiplexer_10_out;  // NOT_Gate not_2, 32 bits wide
  Multiplexer #(.width(32)) multiplexer_7 (
    .in0(controlled_buffer_4_out), .in1({32{1'b0}}), .out(multiplexer_7_out), .sel(1'b0));
  assign xor_2_out = multiplexer_10_out ^ bit_extender_5_out;  // XOR_Gate xor_2, 32 bits wide
  assign controlled_buffer_3_out = decoder_2_out16[0] ? x16_q : 32'bz;  // Controlled_Buffer controlled_buffer_36
  assign controlled_buffer_4_out = decoder_3_out16[0] ? x16_q : 32'bz;  // Controlled_Buffer controlled_buffer_37
  assign controlled_buffer_3_out = decoder_2_out16[1] ? x17_q : 32'bz;  // Controlled_Buffer controlled_buffer_38
  assign controlled_buffer_4_out = decoder_3_out16[1] ? x17_q : 32'bz;  // Controlled_Buffer controlled_buffer_39
  assign controlled_buffer_3_out = decoder_2_out16[2] ? x18_q : 32'bz;  // Controlled_Buffer controlled_buffer_40
  assign controlled_buffer_4_out = decoder_3_out16[2] ? x18_q : 32'bz;  // Controlled_Buffer controlled_buffer_41
  assign controlled_buffer_3_out = decoder_2_out16[3] ? x19_q : 32'bz;  // Controlled_Buffer controlled_buffer_42
  assign controlled_buffer_4_out = decoder_3_out16[3] ? x19_q : 32'bz;  // Controlled_Buffer controlled_buffer_43
  assign controlled_buffer_3_out = decoder_2_out16[4] ? x20_q : 32'bz;  // Controlled_Buffer controlled_buffer_44
  assign controlled_buffer_4_out = decoder_3_out16[4] ? x20_q : 32'bz;  // Controlled_Buffer controlled_buffer_45
  assign controlled_buffer_3_out = decoder_2_out16[5] ? x21_q : 32'bz;  // Controlled_Buffer controlled_buffer_46
  assign controlled_buffer_4_out = decoder_3_out16[5] ? x21_q : 32'bz;  // Controlled_Buffer controlled_buffer_47
  assign controlled_buffer_3_out = decoder_2_out16[6] ? x22_q : 32'bz;  // Controlled_Buffer controlled_buffer_48
  assign controlled_buffer_4_out = decoder_3_out16[6] ? x22_q : 32'bz;  // Controlled_Buffer controlled_buffer_49
  assign controlled_buffer_3_out = decoder_2_out16[7] ? x23_q : 32'bz;  // Controlled_Buffer controlled_buffer_50
  assign controlled_buffer_4_out = decoder_3_out16[7] ? x23_q : 32'bz;  // Controlled_Buffer controlled_buffer_51
  Multiplexer #(.select(2), .width(32)) multiplexer_8 (
    .in0(and_3_out), .in1(or_4_out), .in2(xor_1_out), .in3(not_2_out), .out(multiplexer_8_out), .sel(2'b00));
  Adder #(.width(32)) adder_3 (.a(multiplexer_7_out), .b(xor_2_out), .out(adder_3_out), .cin(1'b0), .cout(out_22[3]));
  Register #(.width(32)) x24 (
    .D(controlled_buffer_1_out), .en(decoder_1_out1[24]), .clk(clock_5_out), .Q(x24_q));  // open: clr
  Register #(.width(32)) x25 (
    .D(controlled_buffer_1_out), .en(decoder_1_out1[25]), .clk(clock_5_out), .Q(x25_q));  // open: clr
  Register #(.width(32)) x26 (
    .D(controlled_buffer_1_out), .en(decoder_1_out1[26]), .clk(clock_5_out), .Q(x26_q));  // open: clr
  Register #(.width(32)) x27 (
    .D(controlled_buffer_1_out), .en(decoder_1_out1[27]), .clk(clock_5_out), .Q(x27_q));  // open: clr
  Register #(.width(32)) x28 (
    .D(controlled_buffer_1_out), .en(decoder_1_out1[28]), .clk(clock_5_out), .Q(x28_q));  // open: clr
  Register #(.width(32)) x29 (
    .D(controlled_buffer_1_out), .en(decoder_1_out1[29]), .clk(clock_5_out), .Q(x29_q));  // open: clr
  Register #(.width(32)) x30 (
    .D(controlled_buffer_1_out), .en(decoder_1_out1[30]), .clk(clock_5_out), .Q(x30_q));  // open: clr
  Register #(.width(32)) x31 (
    .D(controlled_buffer_1_out), .en(decoder_1_out1[31]), .clk(clock_5_out), .Q(x31_q));  // open: clr
  // Probe on {out_22[2], multiplexer_9_out}
  Multiplexer #(.width(32)) multiplexer_9 (
    .in0(multiplexer_8_out), .in1(adder_3_out), .out({out_22[2], multiplexer_9_out}), .sel(1'b0));
  Multiplexer #(.width(32)) multiplexer_10 (
    .in0(controlled_buffer_3_out), .in1(controlled_buffer_1_out), .out(multiplexer_10_out), .sel(in_10));
  assign controlled_buffer_19_out = in_9 ? {out_22[2], multiplexer_9_out} : 32'bz;  // Controlled_Buffer controlled_buffer_52
  assign controlled_buffer_3_out = decoder_2_out24[0] ? x24_q : 32'bz;  // Controlled_Buffer controlled_buffer_53
  assign controlled_buffer_4_out = decoder_3_out24[0] ? x24_q : 32'bz;  // Controlled_Buffer controlled_buffer_54
  assign controlled_buffer_3_out = decoder_2_out24[1] ? x25_q : 32'bz;  // Controlled_Buffer controlled_buffer_55
  assign controlled_buffer_4_out = decoder_3_out24[1] ? x25_q : 32'bz;  // Controlled_Buffer controlled_buffer_56
  assign controlled_buffer_3_out = decoder_2_out24[2] ? x26_q : 32'bz;  // Controlled_Buffer controlled_buffer_57
  assign controlled_buffer_4_out = decoder_3_out24[2] ? x26_q : 32'bz;  // Controlled_Buffer controlled_buffer_58
  assign controlled_buffer_3_out = decoder_2_out24[3] ? x27_q : 32'bz;  // Controlled_Buffer controlled_buffer_59
  assign controlled_buffer_4_out = decoder_3_out24[3] ? x27_q : 32'bz;  // Controlled_Buffer controlled_buffer_60
  assign controlled_buffer_3_out = decoder_2_out24[4] ? x28_q : 32'bz;  // Controlled_Buffer controlled_buffer_61
  assign controlled_buffer_4_out = decoder_3_out24[4] ? x28_q : 32'bz;  // Controlled_Buffer controlled_buffer_62
  assign controlled_buffer_3_out = decoder_2_out24[5] ? x29_q : 32'bz;  // Controlled_Buffer controlled_buffer_63
  assign controlled_buffer_4_out = decoder_3_out24[5] ? x29_q : 32'bz;  // Controlled_Buffer controlled_buffer_64
  assign controlled_buffer_3_out = decoder_2_out24[6] ? x30_q : 32'bz;  // Controlled_Buffer controlled_buffer_65
  assign controlled_buffer_4_out = decoder_3_out24[6] ? x30_q : 32'bz;  // Controlled_Buffer controlled_buffer_66
  assign controlled_buffer_3_out = decoder_2_out24[7] ? x31_q : 32'bz;  // Controlled_Buffer controlled_buffer_67
  assign controlled_buffer_4_out = decoder_3_out24[7] ? x31_q : 32'bz;  // Controlled_Buffer controlled_buffer_68
  xor xor_3 (out_22[0], out_22[3], adder_3_out[31]);
  Decoder #(.select(5)) decoder_2 (
    .out0(decoder_2_out0[0]), .out1(decoder_2_out0[1]), .out2(decoder_2_out0[2]), .out3(decoder_2_out0[3]),
    .out4(decoder_2_out0[4]), .out5(decoder_2_out0[5]), .out6(decoder_2_out0[6]), .out7(decoder_2_out0[7]),
    .out8(decoder_2_out8[0]), .out9(decoder_2_out8[1]), .out10(decoder_2_out8[2]), .out11(decoder_2_out8[3]),
    .out12(decoder_2_out8[4]), .out13(decoder_2_out8[5]), .out14(decoder_2_out8[6]),
    .out15(decoder_2_out8[7]), .out16(decoder_2_out16[0]), .out17(decoder_2_out16[1]),
    .out18(decoder_2_out16[2]), .out19(decoder_2_out16[3]), .out20(decoder_2_out16[4]),
    .out21(decoder_2_out16[5]), .out22(decoder_2_out16[6]), .out23(decoder_2_out16[7]),
    .out24(decoder_2_out24[0]), .out25(decoder_2_out24[1]), .out26(decoder_2_out24[2]),
    .out27(decoder_2_out24[3]), .out28(decoder_2_out24[4]), .out29(decoder_2_out24[5]),
    .out30(decoder_2_out24[6]), .out31(decoder_2_out24[7]), .sel(out_17[19:15]));  // open: en
  Decoder #(.select(5)) decoder_3 (
    .out0(decoder_3_out0[0]), .out1(decoder_3_out0[1]), .out2(decoder_3_out0[2]), .out3(decoder_3_out0[3]),
    .out4(decoder_3_out0[4]), .out5(decoder_3_out0[5]), .out6(decoder_3_out0[6]), .out7(decoder_3_out0[7]),
    .out8(decoder_3_out8[0]), .out9(decoder_3_out8[1]), .out10(decoder_3_out8[2]), .out11(decoder_3_out8[3]),
    .out12(decoder_3_out8[4]), .out13(decoder_3_out8[5]), .out14(decoder_3_out8[6]),
    .out15(decoder_3_out8[7]), .out16(decoder_3_out16[0]), .out17(decoder_3_out16[1]),
    .out18(decoder_3_out16[2]), .out19(decoder_3_out16[3]), .out20(decoder_3_out16[4]),
    .out21(decoder_3_out16[5]), .out22(decoder_3_out16[6]), .out23(decoder_3_out16[7]),
    .out24(decoder_3_out24[0]), .out25(decoder_3_out24[1]), .out26(decoder_3_out24[2]),
    .out27(decoder_3_out24[3]), .out28(decoder_3_out24[4]), .out29(decoder_3_out24[5]),
    .out30(decoder_3_out24[6]), .out31(decoder_3_out24[7]), .sel(out_17[24:20]));  // open: en
  nor nor_1 (out_22[1], out_22[2], multiplexer_9_out[30], multiplexer_9_out[29], multiplexer_9_out[28], multiplexer_9_out[27], multiplexer_9_out[26], multiplexer_9_out[25], multiplexer_9_out[24], multiplexer_9_out[23], multiplexer_9_out[22], multiplexer_9_out[21], multiplexer_9_out[20], multiplexer_9_out[19], multiplexer_9_out[18], multiplexer_9_out[17], multiplexer_9_out[16], multiplexer_9_out[15], multiplexer_9_out[14], multiplexer_9_out[13], multiplexer_9_out[12], multiplexer_9_out[11], multiplexer_9_out[10], multiplexer_9_out[9], multiplexer_9_out[8], multiplexer_9_out[7], multiplexer_9_out[6], multiplexer_9_out[5], multiplexer_9_out[4], multiplexer_9_out[3], multiplexer_9_out[2], multiplexer_9_out[1], multiplexer_9_out[0]);
  Register #(.width(6)) register_1 (.D(undriven), .en(1'b1), .clk(clock_7_out), .Q(register_1_q));  // open: clr
  Clock clock_7 (.out(clock_7_out));
  ROM #(.addrWidth(6), .dataWidth(64)) rom_1 (.addr(register_1_q), .data(rom_1_data));
  not not_3 (not_3_out, in_1);
  assign controlled_buffer_69_out = not_3_out ? rom_1_data[31:0] : 32'bz;  // Controlled_Buffer controlled_buffer_69
  Register #(.width(6)) u_State (.D(register_1_q), .en(1'b1), .clk(clock_8_out), .Q(State), .clr(in_1));
  Register #(.width(32)) register_2 (
    .D(controlled_buffer_69_out), .en(1'b1), .clk(clock_8_out), .Q(Microinstr), .clr(in_1));
  Clock clock_8 (.out(clock_8_out));

  assign out_18 = out_17[6:0];

  // Other names for the same wires on the sheet: ALU_BP = in_10; C_MDR = in_13; CNZV[3:0] = out_22; GateALU = in_9;
  //   GateMAR = in_7; GateMDR = in_8; GatePC = in_3; imm32[31:0] = out_19;
  //   immB[12:1] = {out_17[31], out_17[7], out_17[30:25], out_17[11:8]}; immS[11:0] = {out_17[31:25], out_17[11:7]};
  //   Instr[31:0] = out_17; rd[4:0] = out_17[11:7]; immI[11:0] = out_17[31:20];
  //   immJ[20:1] = {out_17[31], out_17[19:12], out_17[20], out_17[30:21]}; immU[31:12] = out_17[31:12];
  //   rs2[4:0] = out_17[24:20]; funct7[6:0] = out_17[31:25]; funct3[2:0] = out_17[14:12]; rs1[4:0] = out_17[19:15];
  //   SE = out_17[31]; opcode[6:0] = out_17[6:0]; LD_IR = in_5; LD_MAR = in_11; LD_MDR = in_12; LD_PC = in_4;
  //   LD_REG = in_6; MEM_EN = in_15; PC[31:0] = out_16; PCMUX = in_2; R_W = in_14; ResetSim = in_1;
  //   SR1[31:0] = out_20; SR2[31:0] = out_21

  // Notes on the sheet:
  //   R
  //   I
  //   S
  //   B
  //   U
  //   J
  //   Memory
  //   Control Logic
  //   DR
  //   REGISTER FILE
  //   I/O Mem Mapping
  //   ALU_OUT
  //   SR1
  //   SR2
  //   ALU
  //   Control Store
  //   Microsequencer
endmodule
