// Logisim project riscv_simulator_multibus.circ as structural Verilog: 3 circuits, main circuit main
module main (
  input  in_1,
  input  in_2,
  output [31:0] out_3,
  output [31:0] out_4,
  output [6:0] out_5,
  output [31:0] out_6,
  output [31:0] out_7,
  output [31:0] out_8,
  output [31:0] out_9
);

  wire and_1_out, and_2_out, and_3_out, and_4_out, and_5_out, and_6_out, and_7_out, and_12_out, and_13_out,
       BranchOp, clock_2_out, clock_3_out, clock_4_out, clock_5_out, clock_6_out, clock_7_out, clock_8_out,
       comparator_1_eq, comparator_2_eq, comparator_3_eq, comparator_4_eq, comparator_5_eq, comparator_6_eq,
       comparator_7_eq, comparator_8_eq, comparator_9_eq, comparator_10_eq, comparator_11_eq,
       comparator_12_eq, comparator_13_eq, comparator_14_eq, comparator_15_eq, comparator_16_eq,
       comparator_17_eq, comparator_18_eq, comparator_19_eq, comparator_20_eq, comparator_21_eq,
       comparator_22_eq, comparator_23_eq, comparator_24_eq, comparator_25_eq, comparator_26_eq,
       comparator_27_eq, comparator_28_eq, comparator_29_eq, comparator_30_eq, Flush, Flushed_q, IFID_stall,
       LD_R, not_1_out, not_2_out, not_3_out, not_4_out, not_5_out, not_6_out, not_7_out, not_9_out,
       or_1_out, or_2_out, or_3_out, or_4_out, or_5_out, or_6_out, or_7_out, or_8_out, or_9_out, or_10_out,
       or_11_out, or_13_out, PC_TA, priority_encoder_2_out;
  wire [1:0] and_9_out, lu_hzrd, lu_hzrd0, priority_encoder_1_out, register_1_q;
  wire [2:0] decoder_2_out5, decoder_2_out13, decoder_2_out21, decoder_2_out29, decoder_3_out13,
       decoder_3_out21, decoder_3_out29, fd_1_format, fd_2_format, fd_3_format, fd_4_format, funct3;
  wire [4:0] decoder_2_out0, decoder_2_out8, decoder_2_out16, decoder_2_out24, decoder_3_out8,
       decoder_3_out16, decoder_3_out24, immI, rd0, rd1, rd2, rs1_dh0, rs1_dh1, rs2_dh0, rs2_dh1;
  wire [6:0] funct7, op0, op1, op2;
  wire [7:0] decoder_3_out0;
  wire [9:0] funct;
  wire [11:1] immB;
  wire [19:15] immJ;
  wire [23:0] undriven_2;
  wire [31:0] adder_1_out, adder_2_out, adder_3_out, adder_4_out, aluR, aluR1, bit_extender_1_out,
       bit_extender_2_out, bit_extender_3_out, bit_extender_4_out, BranchCond_q, controlled_buffer_1_out,
       controlled_buffer_2_out, divider_1_out, divider_1_rem, divider_2_out, imm0, imm1, MAIN_ALU_alu_out,
       mem, multiplexer_1_out, multiplexer_2_out, multiplexer_3_out, multiplexer_4_out, multiplexer_5_out,
       multiplexer_6_out, multiplexer_7_out, multiplexer_8_out, multiplexer_9_out, multiplexer_10_out,
       multiplexer_11_out, multiplexer_16_out, multiplexer_17_out, multiplexer_18_out, PC0_q, PC1, PC2, PC3,
       PC4_q, S1, S2, SB, TA, TA_ALU_ta_out, undriven, x1_q, x2_q, x3_q, x4_q, x5_q, x6_q, x7_q, x8_q, x9_q,
       x10_q, x11_q, x12_q, x13_q, x14_q, x15_q, x16_q, x17_q, x18_q, x19_q, x20_q, x21_q, x22_q, x23_q,
       x24_q, x25_q, x26_q, x27_q, x28_q, x29_q, x30_q, x31_q;
  wire [31:1] decoder_1_out1;

  Clock clock_1 ();  // open: out
  not not_1 (not_1_out, IFID_stall);
  or or_1 (or_1_out, in_1, not_1_out);
  Multiplexer #(.width(32)) multiplexer_1 (.in0(PC0_q), .in1(PC1), .out(multiplexer_1_out), .sel(IFID_stall));
  Register #(.width(32)) u_PC1 (.D(PC0_q), .en(or_1_out), .clk(clock_2_out), .Q(PC1), .clr(in_1));
  not not_2 (not_2_out, in_1);
  Register #(.width(32)) PC0 (.D(multiplexer_2_out), .en(or_1_out), .clk(clock_2_out), .Q(PC0_q));  // open: clr
  Multiplexer #(.width(32)) multiplexer_2 (
    .in0({32{1'b0}}), .in1(multiplexer_3_out), .out(multiplexer_2_out), .sel(not_2_out));
  Clock clock_2 (.out(clock_2_out));
  Multiplexer #(.width(32)) multiplexer_3 (.in0(adder_1_out), .in1(TA), .out(multiplexer_3_out), .sel(PC_TA));
  Adder #(.width(32)) adder_1 (.a(32'h4), .b(PC0_q), .out(adder_1_out));  // open: cin, cout
  Multiplexer #(.width(32)) multiplexer_4 (.in0(aluR), .in1(aluR1), .out(multiplexer_4_out), .sel(and_6_out));
  Comparator #(.width(5)) comparator_1 (.a(rd1), .b({5{1'b0}}), .eq(comparator_1_eq));  // open: gt, lt
  Comparator #(.width(5)) comparator_2 (.a(rd1), .b(rs1_dh0), .eq(comparator_2_eq));  // open: gt, lt
  Comparator #(.width(5)) comparator_3 (.a(rd1), .b(rs2_dh0), .eq(comparator_3_eq));  // open: gt, lt
  Divider #(.width(32)) divider_1 (
    .a(multiplexer_1_out), .b(32'h4), .out(divider_1_out), .rem(divider_1_rem));  // open: upper
  Multiplexer #(.width(32)) multiplexer_5 (.in0(S2), .in1(multiplexer_4_out), .out(multiplexer_5_out), .sel(or_3_out));
  FD fd_1 (.opcode(op0), .format(fd_1_format));
  not not_3 (not_3_out, comparator_1_eq);
  not not_4 (not_4_out, comparator_4_eq);
  Comparator #(.width(5)) comparator_4 (.a(rd2), .b({5{1'b0}}), .eq(comparator_4_eq));  // open: gt, lt
  Comparator #(.width(5)) comparator_5 (.a(rd2), .b(rs1_dh0), .eq(comparator_5_eq));  // open: gt, lt
  Comparator #(.width(5)) comparator_6 (.a(rd2), .b(rs2_dh0), .eq(comparator_6_eq));  // open: gt, lt
  // ROM #(.addrWidth(24), .dataWidth(32), .line("dual"), .misaligned("true")) InstrCache: pin names not known; wires that end beside it: divider_1_out[23:0]
  Multiplexer #(.width(32)) multiplexer_6 (
    .in0(multiplexer_5_out), .in1(mem), .out(multiplexer_6_out), .sel(lu_hzrd0[1]));
  Multiplexer #(.width(32)) multiplexer_7 (
    .in0(multiplexer_6_out), .in1(imm0), .out(multiplexer_7_out), .sel(or_2_out));
  or or_2 (or_2_out, comparator_7_eq, comparator_8_eq, comparator_9_eq);
  Comparator #(.width(3)) comparator_7 (.a(fd_1_format), .b(3'b001), .eq(comparator_7_eq));  // open: gt, lt
  or or_3 (or_3_out, and_4_out, and_2_out);
  and and_1 (and_1_out, not_3_out, comparator_2_eq);
  and and_2 (and_2_out, not_3_out, comparator_3_eq);
  and and_3 (and_3_out, not_4_out, comparator_5_eq);
  and and_4 (and_4_out, not_4_out, comparator_6_eq);
  Comparator #(.width(7)) comparator_8 (.a(op0), .b(7'b0110111), .eq(comparator_8_eq));  // open: gt, lt
  Comparator #(.width(7)) comparator_9 (.a(op0), .b(7'b0010111), .eq(comparator_9_eq));  // open: gt, lt
  Multiplexer #(.width(32)) multiplexer_8 (.in0(S1), .in1(multiplexer_10_out), .out(multiplexer_8_out), .sel(or_4_out));
  or or_4 (or_4_out, and_1_out, and_3_out);
  ALU TA_ALU (.funct(10'h98), .PC(PC2), .X(imm0), .Y(PC2), .opcode(op0), .ta_out(TA_ALU_ta_out));  // open: alu_out
  ALU MAIN_ALU (
    .funct(funct), .PC(PC2), .X(multiplexer_7_out), .Y(multiplexer_9_out), .opcode(op0),
    .alu_out(MAIN_ALU_alu_out));  // open: ta_out
  Multiplexer #(.width(32)) multiplexer_9 (
    .in0(multiplexer_8_out), .in1(mem), .out(multiplexer_9_out), .sel(lu_hzrd0[0]));
  Multiplexer #(.width(32)) multiplexer_10 (.in0(aluR), .in1(aluR1), .out(multiplexer_10_out), .sel(and_5_out));
  and and_5 (and_5_out, ~and_1_out, and_3_out);  // AND_Gate
  and and_6 (and_6_out, ~and_2_out, and_4_out);  // AND_Gate
  Multiplexer #(.select(3), .width(32)) multiplexer_11 (
    .in0(undriven), .in1({undriven_2[7:0], undriven[31:8]}), .in2({undriven_2[15:0], undriven[31:16]}),
    .in3({undriven_2, undriven[31:24]}), .out(multiplexer_11_out));  // open: in4, in5, in6, in7, sel
  Register #(.width(5)) u_rd1 (.D(rd0), .en(1'b1), .clk(clock_3_out), .Q(rd1), .clr(in_1));
  Register #(.width(7)) u_op1 (.D(op0), .en(1'b1), .clk(clock_3_out), .Q(op1), .clr(in_1));
  Register #(.width(32)) u_PC3 (.D(PC2), .en(1'b1), .clk(clock_3_out), .Q(PC3), .clr(in_1));
  Register #(.width(32)) u_TA (.D(TA_ALU_ta_out), .en(1'b1), .clk(clock_3_out), .Q(TA), .clr(in_1));
  Register #(.width(32)) u_aluR (.D(MAIN_ALU_alu_out), .en(1'b1), .clk(clock_3_out), .Q(aluR), .clr(in_1));
  Register #(.width(32)) u_SB (.D(multiplexer_7_out), .en(1'b1), .clk(clock_3_out), .Q(SB), .clr(in_1));
  Register #(.width(5)) u_rs1_dh1 (.D(rs1_dh0), .en(1'b1), .clk(clock_3_out), .Q(rs1_dh1), .clr(in_1));
  Register #(.width(5)) u_rs2_dh1 (.D(rs2_dh0), .en(1'b1), .clk(clock_3_out), .Q(rs2_dh1), .clr(in_1));
  Register #(.width(32)) u_imm1 (.D(imm0), .en(1'b1), .clk(clock_3_out), .Q(imm1), .clr(in_1));
  Clock clock_3 (.out(clock_3_out));
  Register #(.width(32)) IR (.D(multiplexer_11_out), .en(1'b1), .clk(clock_4_out), .Q(out_4), .clr(or_5_out));
  Clock clock_4 (.out(clock_4_out));
  FD fd_2 (.opcode(op1), .format(fd_2_format));
  Register #(.trigger("falling"), .width(32)) BranchCond (
    .D(aluR), .en(1'b1), .clk(clock_3_out), .Q(BranchCond_q), .clr(in_1));
  or or_5 (or_5_out, in_1, Flush);
  Multiplexer #(.width(32)) multiplexer_12 (
    .in0(out_4), .in1(32'h13), .out({funct7, immI, immJ, funct3, immB[4:1], immB[11], out_5}),
    .sel(IFID_stall));
  Comparator #(.width(7)) comparator_10 (.a(op1), .b(7'b1101111), .eq(comparator_10_eq));  // open: gt, lt
  or or_6 (or_6_out, comparator_10_eq, comparator_11_eq);
  Comparator #(.width(7)) comparator_11 (.a(op1), .b(7'b1100111), .eq(comparator_11_eq));  // open: gt, lt
  Comparator #(.width(3)) comparator_12 (.a(3'b011), .b(fd_2_format), .eq(comparator_12_eq));  // open: gt, lt
  Adder #(.width(32)) adder_2 (.a(PC2), .b(32'h4), .out(adder_2_out));  // open: cin, cout
  Register #(.trigger("falling"), .width(1)) u_BranchOp (
    .D(or_7_out), .en(1'b1), .clk(clock_3_out), .Q(BranchOp), .clr(in_1));
  or or_7 (or_7_out, or_6_out, comparator_12_eq);
  not not_5 (not_5_out, comparator_13_eq);
  Comparator #(.width(32)) comparator_13 (.a(adder_2_out), .b(TA), .eq(comparator_13_eq));  // open: gt, lt
  FD fd_3 (.opcode(out_5), .format(fd_3_format));
  or or_8 (or_8_out, or_6_out, and_7_out);
  and and_7 (and_7_out, not_5_out, BranchCond_q[0]);
  not not_6 (not_6_out, comparator_14_eq);
  Comparator #(.width(5)) comparator_14 (.a(rd0), .b({5{1'b0}}), .eq(comparator_14_eq));  // open: gt, lt
  Comparator #(.width(5)) comparator_15 (.a(rd0), .b(out_4[19:15]), .eq(comparator_15_eq));  // open: gt, lt
  Comparator #(.width(5)) comparator_16 (.a(rd0), .b(out_4[24:20]), .eq(comparator_16_eq));  // open: gt, lt
  and and_8 (PC_TA, BranchOp, or_8_out);
  and and_9 (and_9_out[0], not_6_out, comparator_15_eq);
  and and_10 (and_9_out[1], not_6_out, comparator_16_eq);
  assign bit_extender_1_out = {{20{funct7[6]}}, {funct7, immI}};  // Bit_Extender bit_extender_1
  assign bit_extender_2_out = {{20{funct7[6]}}, {funct7, immB[4:1], immB[11]}};  // Bit_Extender bit_extender_2
  Register #(.width(1)) Flushed (.D(PC_TA), .en(1'b1), .clk(clock_3_out), .Q(Flushed_q), .clr(in_1));
  Multiplexer #(.width(2)) multiplexer_13 (.in0(2'b00), .in1(and_9_out), .out(lu_hzrd), .sel(comparator_17_eq));
  Comparator #(.width(7)) comparator_17 (.a(op0), .b(7'b0000011), .eq(comparator_17_eq));  // open: gt, lt
  Multiplexer #(.select(3), .width(32)) multiplexer_14 (
    .in1(bit_extender_1_out), .in2(bit_extender_2_out), .in3(bit_extender_3_out),
    .in4({funct7, immI, immJ, funct3, {12{1'b0}}}), .in5(bit_extender_4_out), .in7({32{1'b0}}), .out(out_6));  // open: in0, in6, sel
  assign bit_extender_3_out = {{19{funct7[6]}}, {funct7[6], immB[11], funct7[5:0], immB[4:1], 1'b0}};  // Bit_Extender bit_extender_3
  assign bit_extender_4_out = {{11{funct7[6]}}, {funct7[6], immJ, funct3, immI[0], funct7[5:0], immI[4:1], 1'b0}};  // Bit_Extender bit_extender_4
  and and_11 (Flush, PC_TA, not_7_out);
  not not_7 (not_7_out, Flushed_q);
  Comparator #(.width(2)) comparator_18 (.a(2'b00), .b(lu_hzrd), .eq(comparator_18_eq));  // open: gt, lt
  FD fd_4 (.opcode(op1), .format(fd_4_format));
  not not_8 (IFID_stall, comparator_18_eq);
  Comparator #(.width(3)) comparator_19 (.a(fd_4_format), .b(3'b010), .eq(comparator_19_eq));  // open: gt, lt
  Clock clock_5 (.out(clock_5_out));
  Comparator #(.width(3)) comparator_20 (.a(fd_4_format), .b(3'b001), .eq(comparator_20_eq));  // open: gt, lt
  Divider #(.width(32)) divider_2 (.a(aluR), .b(32'h4), .out(divider_2_out));  // open: upper, rem
  RAM #(.addrWidth(24), .clearpin("true"), .dataWidth(32)) DataCache (
    .addr(divider_2_out[23:0]), .we(comparator_19_eq), .oe(comparator_20_eq), .clk(clock_5_out), .din(SB),
    .dout(mem), .clr(in_1));
  Clock clock_6 (.out(clock_6_out));
  Decoder #(.select(5)) decoder_1 (
    .out1(decoder_1_out1[1]), .out2(decoder_1_out1[2]), .out3(decoder_1_out1[3]), .out4(decoder_1_out1[4]),
    .out5(decoder_1_out1[5]), .out6(decoder_1_out1[6]), .out7(decoder_1_out1[7]), .out8(decoder_1_out1[8]),
    .out9(decoder_1_out1[9]), .out10(decoder_1_out1[10]), .out11(decoder_1_out1[11]),
    .out12(decoder_1_out1[12]), .out13(decoder_1_out1[13]), .out14(decoder_1_out1[14]),
    .out15(decoder_1_out1[15]), .out16(decoder_1_out1[16]), .out17(decoder_1_out1[17]),
    .out18(decoder_1_out1[18]), .out19(decoder_1_out1[19]), .out20(decoder_1_out1[20]),
    .out21(decoder_1_out1[21]), .out22(decoder_1_out1[22]), .out23(decoder_1_out1[23]),
    .out24(decoder_1_out1[24]), .out25(decoder_1_out1[25]), .out26(decoder_1_out1[26]),
    .out27(decoder_1_out1[27]), .out28(decoder_1_out1[28]), .out29(decoder_1_out1[29]),
    .out30(decoder_1_out1[30]), .out31(decoder_1_out1[31]), .sel(rd2), .en(LD_R));  // open: out0
  Register #(.width(32)) x1 (.D(out_9), .en(decoder_1_out1[1]), .clk(clock_6_out), .Q(x1_q), .clr(in_1));
  Register #(.width(32)) x2 (.D(out_9), .en(decoder_1_out1[2]), .clk(clock_6_out), .Q(x2_q), .clr(in_1));
  Register #(.width(32)) x3 (.D(out_9), .en(decoder_1_out1[3]), .clk(clock_6_out), .Q(x3_q), .clr(in_1));
  Register #(.width(32)) x4 (.D(out_9), .en(decoder_1_out1[4]), .clk(clock_6_out), .Q(x4_q), .clr(in_1));
  Register #(.width(32)) x5 (.D(out_9), .en(decoder_1_out1[5]), .clk(clock_6_out), .Q(x5_q), .clr(in_1));
  Register #(.width(32)) x6 (.D(out_9), .en(decoder_1_out1[6]), .clk(clock_6_out), .Q(x6_q), .clr(in_1));
  Register #(.width(32)) x7 (.D(out_9), .en(decoder_1_out1[7]), .clk(clock_6_out), .Q(x7_q), .clr(in_1));
  assign controlled_buffer_1_out = decoder_2_out0[0] ? {32{1'b0}} : 32'bz;  // Controlled_Buffer controlled_buffer_1
  assign controlled_buffer_2_out = decoder_3_out0[0] ? {32{1'b0}} : 32'bz;  // Controlled_Buffer controlled_buffer_2
  assign controlled_buffer_1_out = decoder_2_out0[1] ? x1_q : 32'bz;  // Controlled_Buffer controlled_buffer_3
  assign controlled_buffer_2_out = decoder_3_out0[1] ? x1_q : 32'bz;  // Controlled_Buffer controlled_buffer_4
  assign controlled_buffer_1_out = decoder_2_out0[2] ? x2_q : 32'bz;  // Controlled_Buffer controlled_buffer_5
  assign controlled_buffer_2_out = decoder_3_out0[2] ? x2_q : 32'bz;  // Controlled_Buffer controlled_buffer_6
  assign controlled_buffer_1_out = decoder_2_out0[3] ? x3_q : 32'bz;  // Controlled_Buffer controlled_buffer_7
  assign controlled_buffer_2_out = decoder_3_out0[3] ? x3_q : 32'bz;  // Controlled_Buffer controlled_buffer_8
  assign controlled_buffer_1_out = decoder_2_out0[4] ? x4_q : 32'bz;  // Controlled_Buffer controlled_buffer_9
  assign controlled_buffer_2_out = decoder_3_out0[4] ? x4_q : 32'bz;  // Controlled_Buffer controlled_buffer_10
  assign controlled_buffer_1_out = decoder_2_out5[0] ? x5_q : 32'bz;  // Controlled_Buffer controlled_buffer_11
  assign controlled_buffer_2_out = decoder_3_out0[5] ? x5_q : 32'bz;  // Controlled_Buffer controlled_buffer_12
  assign controlled_buffer_1_out = decoder_2_out5[1] ? x6_q : 32'bz;  // Controlled_Buffer controlled_buffer_13
  assign controlled_buffer_2_out = decoder_3_out0[6] ? x6_q : 32'bz;  // Controlled_Buffer controlled_buffer_14
  assign controlled_buffer_1_out = decoder_2_out5[2] ? x7_q : 32'bz;  // Controlled_Buffer controlled_buffer_15
  assign controlled_buffer_2_out = decoder_3_out0[7] ? x7_q : 32'bz;  // Controlled_Buffer controlled_buffer_16
  Register #(.width(32)) PC4 (.D(PC3), .en(1'b1), .clk(clock_7_out), .Q(PC4_q), .clr(in_1));
  Register #(.width(32)) u_aluR1 (.D(aluR), .en(1'b1), .clk(clock_7_out), .Q(aluR1), .clr(in_1));
  Register #(.width(7)) u_op2 (.D(op1), .en(1'b1), .clk(clock_7_out), .Q(op2), .clr(in_1));
  Register #(.width(5)) u_rd2 (.D(rd1), .en(1'b1), .clk(clock_7_out), .Q(rd2), .clr(in_1));
  Clock clock_7 (.out(clock_7_out));
  Register #(.width(32)) x8 (.D(out_9), .en(decoder_1_out1[8]), .clk(clock_6_out), .Q(x8_q), .clr(in_1));
  Register #(.width(32)) x9 (.D(out_9), .en(decoder_1_out1[9]), .clk(clock_6_out), .Q(x9_q), .clr(in_1));
  Register #(.width(32)) x10 (.D(out_9), .en(decoder_1_out1[10]), .clk(clock_6_out), .Q(x10_q), .clr(in_1));
  Register #(.width(32)) x11 (.D(out_9), .en(decoder_1_out1[11]), .clk(clock_6_out), .Q(x11_q), .clr(in_1));
  Register #(.width(32)) x12 (.D(out_9), .en(decoder_1_out1[12]), .clk(clock_6_out), .Q(x12_q), .clr(in_1));
  Register #(.width(32)) x13 (.D(out_9), .en(decoder_1_out1[13]), .clk(clock_6_out), .Q(x13_q), .clr(in_1));
  Register #(.width(32)) x14 (.D(out_9), .en(decoder_1_out1[14]), .clk(clock_6_out), .Q(x14_q), .clr(in_1));
  Register #(.width(32)) x15 (.D(out_9), .en(decoder_1_out1[15]), .clk(clock_6_out), .Q(x15_q), .clr(in_1));
  assign controlled_buffer_1_out = decoder_2_out8[0] ? x8_q : 32'bz;  // Controlled_Buffer controlled_buffer_17
  assign controlled_buffer_1_out = decoder_2_out8[1] ? x9_q : 32'bz;  // Controlled_Buffer controlled_buffer_18
  assign controlled_buffer_1_out = decoder_2_out8[2] ? x10_q : 32'bz;  // Controlled_Buffer controlled_buffer_19
  assign controlled_buffer_1_out = decoder_2_out8[3] ? x11_q : 32'bz;  // Controlled_Buffer controlled_buffer_20
  assign controlled_buffer_1_out = decoder_2_out8[4] ? x12_q : 32'bz;  // Controlled_Buffer controlled_buffer_21
  assign controlled_buffer_1_out = decoder_2_out13[0] ? x13_q : 32'bz;  // Controlled_Buffer controlled_buffer_22
  assign controlled_buffer_1_out = decoder_2_out13[1] ? x14_q : 32'bz;  // Controlled_Buffer controlled_buffer_23
  assign controlled_buffer_1_out = decoder_2_out13[2] ? x15_q : 32'bz;  // Controlled_Buffer controlled_buffer_24
  Adder #(.width(32)) adder_3 (.a(PC4_q), .b(32'h4), .out(adder_3_out));  // open: cin, cout
  Comparator #(.width(7)) comparator_21 (.a(op2), .b(7'b1101111), .eq(comparator_21_eq));  // open: gt, lt
  Comparator #(.width(7)) comparator_22 (.a(op2), .b(7'b1100111), .eq(comparator_22_eq));  // open: gt, lt
  Comparator #(.width(7)) comparator_23 (.a(op2), .b(7'b0110011), .eq(comparator_23_eq));  // open: gt, lt
  Comparator #(.width(7)) comparator_24 (.a(op2), .b(7'b0010011), .eq(comparator_24_eq));  // open: gt, lt
  Comparator #(.width(7)) comparator_25 (.a(op2), .b(7'b0100011), .eq(comparator_25_eq));  // open: gt, lt
  Comparator #(.width(7)) comparator_26 (.a(op2), .b(7'b0110111), .eq(comparator_26_eq));  // open: gt, lt
  Comparator #(.width(7)) comparator_27 (.a(op2), .b(7'b0010111), .eq(comparator_27_eq));  // open: gt, lt
  assign controlled_buffer_2_out = decoder_3_out8[0] ? x8_q : 32'bz;  // Controlled_Buffer controlled_buffer_25
  assign controlled_buffer_2_out = decoder_3_out8[1] ? x9_q : 32'bz;  // Controlled_Buffer controlled_buffer_26
  assign controlled_buffer_2_out = decoder_3_out8[2] ? x10_q : 32'bz;  // Controlled_Buffer controlled_buffer_27
  assign controlled_buffer_2_out = decoder_3_out8[3] ? x11_q : 32'bz;  // Controlled_Buffer controlled_buffer_28
  assign controlled_buffer_2_out = decoder_3_out8[4] ? x12_q : 32'bz;  // Controlled_Buffer controlled_buffer_29
  assign controlled_buffer_2_out = decoder_3_out13[0] ? x13_q : 32'bz;  // Controlled_Buffer controlled_buffer_30
  assign controlled_buffer_2_out = decoder_3_out13[1] ? x14_q : 32'bz;  // Controlled_Buffer controlled_buffer_31
  assign controlled_buffer_2_out = decoder_3_out13[2] ? x15_q : 32'bz;  // Controlled_Buffer controlled_buffer_32
  Multiplexer #(.select(2), .width(32)) multiplexer_15 (
    .in0(adder_3_out), .in1(aluR1), .in2(mem), .in3(multiplexer_16_out), .out(out_9));  // open: sel
  Multiplexer #(.width(32)) multiplexer_16 (
    .in0(imm1), .in1(adder_4_out), .out(multiplexer_16_out), .sel(priority_encoder_2_out));
  or or_9 (or_9_out, comparator_21_eq, comparator_22_eq);
  or or_10 (or_10_out, comparator_23_eq, comparator_24_eq);
  or or_11 (or_11_out, comparator_26_eq, comparator_27_eq);
  Register #(.width(32)) x16 (.D(out_9), .en(decoder_1_out1[16]), .clk(clock_6_out), .Q(x16_q), .clr(in_1));
  Register #(.width(32)) x17 (.D(out_9), .en(decoder_1_out1[17]), .clk(clock_6_out), .Q(x17_q), .clr(in_1));
  Register #(.width(32)) x18 (.D(out_9), .en(decoder_1_out1[18]), .clk(clock_6_out), .Q(x18_q), .clr(in_1));
  Register #(.width(32)) x19 (.D(out_9), .en(decoder_1_out1[19]), .clk(clock_6_out), .Q(x19_q), .clr(in_1));
  Register #(.width(32)) x20 (.D(out_9), .en(decoder_1_out1[20]), .clk(clock_6_out), .Q(x20_q), .clr(in_1));
  Register #(.width(32)) x21 (.D(out_9), .en(decoder_1_out1[21]), .clk(clock_6_out), .Q(x21_q), .clr(in_1));
  Register #(.width(32)) x22 (.D(out_9), .en(decoder_1_out1[22]), .clk(clock_6_out), .Q(x22_q), .clr(in_1));
  Register #(.width(32)) x23 (.D(out_9), .en(decoder_1_out1[23]), .clk(clock_6_out), .Q(x23_q), .clr(in_1));
  Priority_Encoder #(.select(2)) priority_encoder_1 (
    .in0(or_9_out), .in1(or_10_out), .in2(comparator_25_eq), .in3(or_11_out), .out(priority_encoder_1_out));  // open: gs, en_out, en_in
  Priority_Encoder #(.select(1)) priority_encoder_2 (
    .in0(comparator_26_eq), .in1(comparator_27_eq), .out(priority_encoder_2_out));  // open: gs, en_out, en_in
  assign controlled_buffer_1_out = decoder_2_out16[0] ? x16_q : 32'bz;  // Controlled_Buffer controlled_buffer_33
  assign controlled_buffer_2_out = decoder_3_out16[0] ? x16_q : 32'bz;  // Controlled_Buffer controlled_buffer_34
  assign controlled_buffer_1_out = decoder_2_out16[1] ? x17_q : 32'bz;  // Controlled_Buffer controlled_buffer_35
  assign controlled_buffer_2_out = decoder_3_out16[1] ? x17_q : 32'bz;  // Controlled_Buffer controlled_buffer_36
  assign controlled_buffer_1_out = decoder_2_out16[2] ? x18_q : 32'bz;  // Controlled_Buffer controlled_buffer_37
  assign controlled_buffer_2_out = decoder_3_out16[2] ? x18_q : 32'bz;  // Controlled_Buffer controlled_buffer_38
  assign controlled_buffer_1_out = decoder_2_out16[3] ? x19_q : 32'bz;  // Controlled_Buffer controlled_buffer_39
  assign controlled_buffer_2_out = decoder_3_out16[3] ? x19_q : 32'bz;  // Controlled_Buffer controlled_buffer_40
  assign controlled_buffer_1_out = decoder_2_out16[4] ? x20_q : 32'bz;  // Controlled_Buffer controlled_buffer_41
  assign controlled_buffer_2_out = decoder_3_out16[4] ? x20_q : 32'bz;  // Controlled_Buffer controlled_buffer_42
  assign controlled_buffer_1_out = decoder_2_out21[0] ? x21_q : 32'bz;  // Controlled_Buffer controlled_buffer_43
  assign controlled_buffer_2_out = decoder_3_out21[0] ? x21_q : 32'bz;  // Controlled_Buffer controlled_buffer_44
  assign controlled_buffer_1_out = decoder_2_out21[1] ? x22_q : 32'bz;  // Controlled_Buffer controlled_buffer_45
  assign controlled_buffer_2_out = decoder_3_out21[1] ? x22_q : 32'bz;  // Controlled_Buffer controlled_buffer_46
  assign controlled_buffer_1_out = decoder_2_out21[2] ? x23_q : 32'bz;  // Controlled_Buffer controlled_buffer_47
  assign controlled_buffer_2_out = decoder_3_out21[2] ? x23_q : 32'bz;  // Controlled_Buffer controlled_buffer_48
  Adder #(.width(32)) adder_4 (.a(imm1), .b(PC4_q), .out(adder_4_out));  // open: cin, cout
  or or_12 (LD_R, or_9_out, or_10_out, comparator_25_eq, or_11_out);
  Register #(.width(32)) x24 (.D(out_9), .en(decoder_1_out1[24]), .clk(clock_6_out), .Q(x24_q), .clr(in_1));
  Register #(.width(32)) x25 (.D(out_9), .en(decoder_1_out1[25]), .clk(clock_6_out), .Q(x25_q), .clr(in_1));
  Register #(.width(32)) x26 (.D(out_9), .en(decoder_1_out1[26]), .clk(clock_6_out), .Q(x26_q), .clr(in_1));
  Register #(.width(32)) x27 (.D(out_9), .en(decoder_1_out1[27]), .clk(clock_6_out), .Q(x27_q), .clr(in_1));
  Register #(.width(32)) x28 (.D(out_9), .en(decoder_1_out1[28]), .clk(clock_6_out), .Q(x28_q), .clr(in_1));
  Register #(.width(32)) x29 (.D(out_9), .en(decoder_1_out1[29]), .clk(clock_6_out), .Q(x29_q), .clr(in_1));
  Register #(.width(32)) x30 (.D(out_9), .en(decoder_1_out1[30]), .clk(clock_6_out), .Q(x30_q), .clr(in_1));
  Register #(.width(32)) x31 (.D(out_9), .en(decoder_1_out1[31]), .clk(clock_6_out), .Q(x31_q), .clr(in_1));
  assign controlled_buffer_1_out = decoder_2_out24[0] ? x24_q : 32'bz;  // Controlled_Buffer controlled_buffer_49
  assign controlled_buffer_2_out = decoder_3_out24[0] ? x24_q : 32'bz;  // Controlled_Buffer controlled_buffer_50
  assign controlled_buffer_1_out = decoder_2_out24[1] ? x25_q : 32'bz;  // Controlled_Buffer controlled_buffer_51
  assign controlled_buffer_2_out = decoder_3_out24[1] ? x25_q : 32'bz;  // Controlled_Buffer controlled_buffer_52
  assign controlled_buffer_1_out = decoder_2_out24[2] ? x26_q : 32'bz;  // Controlled_Buffer controlled_buffer_53
  assign controlled_buffer_2_out = decoder_3_out24[2] ? x26_q : 32'bz;  // Controlled_Buffer controlled_buffer_54
  assign controlled_buffer_1_out = decoder_2_out24[3] ? x27_q : 32'bz;  // Controlled_Buffer controlled_buffer_55
  assign controlled_buffer_2_out = decoder_3_out24[3] ? x27_q : 32'bz;  // Controlled_Buffer controlled_buffer_56
  assign controlled_buffer_1_out = decoder_2_out24[4] ? x28_q : 32'bz;  // Controlled_Buffer controlled_buffer_57
  assign controlled_buffer_2_out = decoder_3_out24[4] ? x28_q : 32'bz;  // Controlled_Buffer controlled_buffer_58
  assign controlled_buffer_1_out = decoder_2_out29[0] ? x29_q : 32'bz;  // Controlled_Buffer controlled_buffer_59
  assign controlled_buffer_2_out = decoder_3_out29[0] ? x29_q : 32'bz;  // Controlled_Buffer controlled_buffer_60
  assign controlled_buffer_1_out = decoder_2_out29[1] ? x30_q : 32'bz;  // Controlled_Buffer controlled_buffer_61
  assign controlled_buffer_2_out = decoder_3_out29[1] ? x30_q : 32'bz;  // Controlled_Buffer controlled_buffer_62
  assign controlled_buffer_1_out = decoder_2_out29[2] ? x31_q : 32'bz;  // Controlled_Buffer controlled_buffer_63
  assign controlled_buffer_2_out = decoder_3_out29[2] ? x31_q : 32'bz;  // Controlled_Buffer controlled_buffer_64
  Decoder #(.select(5)) decoder_2 (
    .out0(decoder_2_out0[0]), .out1(decoder_2_out0[1]), .out2(decoder_2_out0[2]), .out3(decoder_2_out0[3]),
    .out4(decoder_2_out0[4]), .out5(decoder_2_out5[0]), .out6(decoder_2_out5[1]), .out7(decoder_2_out5[2]),
    .out8(decoder_2_out8[0]), .out9(decoder_2_out8[1]), .out10(decoder_2_out8[2]), .out11(decoder_2_out8[3]),
    .out12(decoder_2_out8[4]), .out13(decoder_2_out13[0]), .out14(decoder_2_out13[1]),
    .out15(decoder_2_out13[2]), .out16(decoder_2_out16[0]), .out17(decoder_2_out16[1]),
    .out18(decoder_2_out16[2]), .out19(decoder_2_out16[3]), .out20(decoder_2_out16[4]),
    .out21(decoder_2_out21[0]), .out22(decoder_2_out21[1]), .out23(decoder_2_out21[2]),
    .out24(decoder_2_out24[0]), .out25(decoder_2_out24[1]), .out26(decoder_2_out24[2]),
    .out27(decoder_2_out24[3]), .out28(decoder_2_out24[4]), .out29(decoder_2_out29[0]),
    .out30(decoder_2_out29[1]), .out31(decoder_2_out29[2]), .sel(immJ));  // open: en
  Decoder #(.select(5)) decoder_3 (
    .out0(decoder_3_out0[0]), .out1(decoder_3_out0[1]), .out2(decoder_3_out0[2]), .out3(decoder_3_out0[3]),
    .out4(decoder_3_out0[4]), .out5(decoder_3_out0[5]), .out6(decoder_3_out0[6]), .out7(decoder_3_out0[7]),
    .out8(decoder_3_out8[0]), .out9(decoder_3_out8[1]), .out10(decoder_3_out8[2]), .out11(decoder_3_out8[3]),
    .out12(decoder_3_out8[4]), .out13(decoder_3_out13[0]), .out14(decoder_3_out13[1]),
    .out15(decoder_3_out13[2]), .out16(decoder_3_out16[0]), .out17(decoder_3_out16[1]),
    .out18(decoder_3_out16[2]), .out19(decoder_3_out16[3]), .out20(decoder_3_out16[4]),
    .out21(decoder_3_out21[0]), .out22(decoder_3_out21[1]), .out23(decoder_3_out21[2]),
    .out24(decoder_3_out24[0]), .out25(decoder_3_out24[1]), .out26(decoder_3_out24[2]),
    .out27(decoder_3_out24[3]), .out28(decoder_3_out24[4]), .out29(decoder_3_out29[0]),
    .out30(decoder_3_out29[1]), .out31(decoder_3_out29[2]), .sel(immI));  // open: en
  Comparator #(.width(5)) comparator_28 (.a(rd2), .b({5{1'b0}}), .eq(comparator_28_eq));  // open: gt, lt
  Comparator #(.width(5)) comparator_29 (.a(rd2), .b(immI), .eq(comparator_29_eq));  // open: gt, lt
  Comparator #(.width(5)) comparator_30 (.a(rd2), .b(immJ), .eq(comparator_30_eq));  // open: gt, lt
  not not_9 (not_9_out, comparator_28_eq);
  and and_12 (and_12_out, not_9_out, comparator_29_eq);
  and and_13 (and_13_out, not_9_out, comparator_30_eq);
  Multiplexer #(.width(32)) multiplexer_17 (
    .in0(controlled_buffer_2_out), .in1(aluR1), .out(multiplexer_17_out), .sel(and_12_out));
  Multiplexer #(.width(32)) multiplexer_18 (
    .in0(controlled_buffer_1_out), .in1(aluR1), .out(multiplexer_18_out), .sel(and_13_out));
  Register #(.width(2)) register_1 (.D(lu_hzrd), .en(1'b1), .clk(clock_8_out), .Q(register_1_q), .clr(or_13_out));
  Register #(.width(2)) u_lu_hzrd (.D(register_1_q), .en(1'b1), .clk(clock_8_out), .Q(lu_hzrd0), .clr(or_13_out));
  Register #(.width(5)) u_rs1_dh0 (.D(immJ), .en(1'b1), .clk(clock_8_out), .Q(rs1_dh0), .clr(or_13_out));
  Register #(.width(5)) u_rs2_dh0 (.D(immI), .en(1'b1), .clk(clock_8_out), .Q(rs2_dh0), .clr(or_13_out));
  Register #(.width(32)) u_imm0 (.D(out_6), .en(1'b1), .clk(clock_8_out), .Q(imm0), .clr(or_13_out));
  Register #(.width(32)) u_PC2 (.D(PC1), .en(1'b1), .clk(clock_8_out), .Q(PC2), .clr(or_13_out));
  Register #(.width(5)) u_rd0 (.D({immB[4:1], immB[11]}), .en(1'b1), .clk(clock_8_out), .Q(rd0), .clr(or_13_out));
  Register #(.width(7)) u_op0 (.D(out_5), .en(1'b1), .clk(clock_8_out), .Q(op0), .clr(or_13_out));
  Register #(.width(10)) u_funct (.D({funct7, funct3}), .en(1'b1), .clk(clock_8_out), .Q(funct), .clr(or_13_out));
  Register #(.width(32)) u_S2 (.D(multiplexer_17_out), .en(1'b1), .clk(clock_8_out), .Q(S2), .clr(or_13_out));
  Register #(.width(32)) u_S1 (.D(multiplexer_18_out), .en(1'b1), .clk(clock_8_out), .Q(S1), .clr(or_13_out));
  Clock clock_8 (.out(clock_8_out));
  or or_13 (or_13_out, in_1, Flush);

  // Other names for the same wires on the sheet: opcode[6:0] = out_5;
  //   immJ (some bits) = {funct7[6], funct3, immI[0], funct7[5:0], immI[4:1]};
  //   immU[31:12] = {funct7, immI, immJ, funct3}; immB (some bits) = funct7; immI[11:5] = funct7;
  //   immS[11:0] = {funct7, immB[4:1], immB[11]}; SE = funct7[6]; imm32[31:0] = out_6;
  //   rd[4:0] = {immB[4:1], immB[11]}; rs2[4:0] = immI; rs1[4:0] = immJ; Instr[31:0] = out_4; PC[31:0] = out_3;
  //   WB_rd[4:0] = rd2; ResetSim = in_1; SR1[31:0] = out_7; SR2[31:0] = out_8; testing = in_2; WB_val[31:0] = out_9

  // Notes on the sheet:
  //   RAW EX hazard detection
  //   RAW WB hazard detection
  //   contents of InstrCache (hex, n*v repeats v):
  //   a137 a097
  //   Byte-addressability
  //   Jumps
  //   rs1
  //   rs2
  //   load-use hazard detection
  //   DR
  //   REGISTER FILE
  //   SR1
  //   SR2
  //   RAW WB hazard detection
endmodule

module ALU (
  input  [31:0] PC,
  input  [6:0] opcode,
  input  [9:0] funct,
  input  [31:0] X,
  input  [31:0] Y,
  output [31:0] ta_out,
  output [31:0] alu_out
);

  wire comparator_1_lt, comparator_2_lt, comparator_3_eq, comparator_4_eq, comparator_5_gt, comparator_6_eq,
       comparator_6_lt, comparator_7_gt, comparator_8_eq, comparator_8_lt, comparator_9_eq, comparator_10_eq,
       comparator_11_eq, comparator_12_eq, comparator_13_eq, multiplexer_6_out, nor_1_out, nor_2_out,
       not_1_out, or_2_out, or_3_out;
  wire [31:0] adder_1_out, adder_2_out, adder_3_out, adder_4_out, adder_5_out, and_1_out, bit_extender_1_out,
       bit_extender_2_out, bit_extender_3_out, multiplexer_1_out, multiplexer_2_out, multiplexer_3_out,
       multiplexer_4_out, multiplexer_5_out, multiplexer_7_out, multiplexer_8_out, or_1_out, shifter_1_out,
       shifter_2_out, shifter_3_out, subtractor_1_out, xor_1_out;

  Adder #(.width(32)) adder_1 (.a(X), .b(Y), .out(adder_1_out));  // open: cin, cout
  Subtractor #(.width(32)) subtractor_1 (.a(X), .b(Y), .out(subtractor_1_out));  // open: bin, bout
  Shifter #(.width(32)) shifter_1 (.in(X), .\dist (Y[4:0]), .out(shifter_1_out));
  Comparator #(.width(32)) comparator_1 (.a(X), .b(Y), .lt(comparator_1_lt));  // open: gt, eq
  Comparator #(.width(32)) comparator_2 (.a(X), .b(Y), .lt(comparator_2_lt));  // open: gt, eq
  assign xor_1_out = X ^ Y;  // XOR_Gate xor_1, 32 bits wide
  Shifter #(.shift("lr"), .width(32)) shifter_2 (.in(X), .\dist (Y[4:0]), .out(shifter_2_out));
  Shifter #(.shift("ar"), .width(32)) shifter_3 (.in(X), .\dist (Y[4:0]), .out(shifter_3_out));
  assign or_1_out = X | Y;  // OR_Gate or_1, 32 bits wide
  assign and_1_out = X & Y;  // AND_Gate and_1, 32 bits wide
  Comparator #(.width(32)) comparator_3 (.a(X), .b(Y), .eq(comparator_3_eq));  // open: gt, lt
  Comparator #(.width(32)) comparator_4 (.a(X), .b(Y), .eq(comparator_4_eq));  // open: gt, lt
  Comparator #(.width(32)) comparator_5 (.a(X), .b(Y), .gt(comparator_5_gt));  // open: eq, lt
  Comparator #(.width(32)) comparator_6 (.a(X), .b(Y), .eq(comparator_6_eq), .lt(comparator_6_lt));  // open: gt
  Comparator #(.mode("unsigned"), .width(32)) comparator_7 (.a(X), .b(Y), .gt(comparator_7_gt));  // open: eq, lt
  Comparator #(.mode("unsigned"), .width(32)) comparator_8 (
    .a(X), .b(Y), .eq(comparator_8_eq), .lt(comparator_8_lt));  // open: gt
  Multiplexer #(.width(32)) multiplexer_1 (
    .in0(adder_1_out), .in1(subtractor_1_out), .out(multiplexer_1_out), .sel(funct[8]));
  assign bit_extender_1_out = {{31{comparator_1_lt}}, comparator_1_lt};  // Bit_Extender bit_extender_1
  assign bit_extender_2_out = {{31{1'b0}}, comparator_2_lt};  // Bit_Extender bit_extender_2
  Multiplexer #(.width(32)) multiplexer_2 (
    .in0(shifter_2_out), .in1(shifter_3_out), .out(multiplexer_2_out), .sel(funct[8]));
  not not_1 (not_1_out, comparator_4_eq);
  or or_2 (or_2_out, comparator_6_eq, comparator_6_lt);
  or or_3 (or_3_out, comparator_8_eq, comparator_8_lt);
  Adder #(.width(32)) adder_2 (.a(X), .b(PC), .out(adder_2_out));  // open: cin, cout
  Adder #(.width(32)) adder_3 (.a(X), .b(Y), .out(adder_3_out));  // open: cin, cout
  Comparator #(.width(7)) comparator_9 (.a(opcode), .b(7'b1101111), .eq(comparator_9_eq));  // open: gt, lt
  Comparator #(.width(7)) comparator_10 (.a(opcode), .b(7'b1100111), .eq(comparator_10_eq));  // open: gt, lt
  Comparator #(.width(7)) comparator_11 (.a(opcode), .b(7'b0110111), .eq(comparator_11_eq));  // open: gt, lt
  Comparator #(.width(7)) comparator_12 (.a(opcode), .b(7'b0010111), .eq(comparator_12_eq));  // open: gt, lt
  Comparator #(.width(7)) comparator_13 (.a(opcode), .b(7'b1100011), .eq(comparator_13_eq));  // open: gt, lt
  Multiplexer #(.select(3), .width(32)) multiplexer_3 (
    .in0(multiplexer_1_out), .in1(shifter_1_out), .in2(bit_extender_1_out), .in3(bit_extender_2_out),
    .in4(xor_1_out), .in5(multiplexer_2_out), .in6(or_1_out), .in7(and_1_out), .out(multiplexer_3_out));  // open: sel
  Multiplexer #(.width(32)) multiplexer_4 (
    .in0(adder_2_out), .in1(adder_3_out), .out(multiplexer_4_out), .sel(comparator_10_eq));
  Adder #(.width(32)) adder_4 (.a(PC), .b(X), .out(adder_4_out));  // open: cin, cout
  Multiplexer #(.width(32)) multiplexer_5 (.in0(X), .in1(adder_4_out), .out(multiplexer_5_out), .sel(comparator_12_eq));
  Adder #(.width(32)) adder_5 (.a(PC), .b(32'h4), .out(adder_5_out));  // open: cin, cout
  assign bit_extender_3_out = {{31{1'b0}}, multiplexer_6_out};  // Bit_Extender bit_extender_3
  Multiplexer #(.select(3)) multiplexer_6 (
    .in0(comparator_3_eq), .in1(not_1_out), .in4(comparator_5_gt), .in5(or_2_out), .in6(comparator_7_gt),
    .in7(or_3_out), .out(multiplexer_6_out));  // open: in2, in3, sel
  nor nor_1 (nor_1_out, comparator_9_eq, comparator_10_eq);
  nor nor_2 (nor_2_out, comparator_11_eq, comparator_12_eq);
  Multiplexer #(.width(32)) multiplexer_7 (
    .in0(multiplexer_5_out), .in1(multiplexer_8_out), .out(multiplexer_7_out), .sel(nor_2_out));
  Multiplexer #(.width(32)) multiplexer_8 (
    .in0(multiplexer_3_out), .in1(bit_extender_3_out), .out(multiplexer_8_out), .sel(comparator_13_eq));
  Multiplexer #(.width(32)) multiplexer_9 (.in0(adder_5_out), .in1(multiplexer_7_out), .out(alu_out), .sel(nor_1_out));
  Multiplexer #(.width(32)) multiplexer_10 (
    .in0(multiplexer_4_out), .in1(multiplexer_1_out), .out(ta_out), .sel(nor_1_out));

  // Other names for the same wires on the sheet: funct3[2:0] = funct[2:0]; funct7[6:0] = funct[9:3]

  // Notes on the sheet:
  //   Arithmetic
  //   Branch Conditions
  //   Jump Targets
  //   Address Construction
endmodule

module FD (
  input  [6:0] opcode,
  output [2:0] format
);

  wire comparator_1_eq, comparator_2_eq, comparator_3_eq, comparator_4_eq, comparator_5_eq, comparator_6_eq,
       comparator_7_eq, comparator_8_eq, comparator_9_eq, comparator_10_eq, comparator_11_eq,
       comparator_12_eq, or_1_out, or_2_out;

  Comparator #(.width(7)) comparator_1 (.a(opcode), .b(7'b0110011), .eq(comparator_1_eq));  // open: gt, lt
  Comparator #(.width(7)) comparator_2 (.a(opcode), .b(7'b0010011), .eq(comparator_2_eq));  // open: gt, lt
  Comparator #(.width(7)) comparator_3 (.a(opcode), .b(7'b0000011), .eq(comparator_3_eq));  // open: gt, lt
  Comparator #(.width(7)) comparator_4 (.a(opcode), .b(7'b1100111), .eq(comparator_4_eq));  // open: gt, lt
  Comparator #(.width(7)) comparator_5 (.a(opcode), .b(7'b1110011), .eq(comparator_5_eq));  // open: gt, lt
  Comparator #(.width(7)) comparator_6 (.a(opcode), .b(7'b0001111), .eq(comparator_6_eq));  // open: gt, lt
  Comparator #(.width(7)) comparator_7 (.a(opcode), .b(7'b0100011), .eq(comparator_7_eq));  // open: gt, lt
  Comparator #(.width(7)) comparator_8 (.a(opcode), .b(7'b1100011), .eq(comparator_8_eq));  // open: gt, lt
  Comparator #(.width(7)) comparator_9 (.a(opcode), .b(7'b0110111), .eq(comparator_9_eq));  // open: gt, lt
  Comparator #(.width(7)) comparator_10 (.a(opcode), .b(7'b0010111), .eq(comparator_10_eq));  // open: gt, lt
  Comparator #(.width(7)) comparator_11 (.a(opcode), .b(7'b1101111), .eq(comparator_11_eq));  // open: gt, lt
  Comparator #(.width(7)) comparator_12 (.a(opcode), .b({7{1'b0}}), .eq(comparator_12_eq));  // open: gt, lt
  or or_1 (or_1_out, comparator_2_eq, comparator_3_eq, comparator_4_eq, comparator_5_eq, comparator_6_eq);
  or or_2 (or_2_out, comparator_9_eq, comparator_10_eq);
  Priority_Encoder priority_encoder_1 (
    .in0(comparator_1_eq), .in1(or_1_out), .in2(comparator_7_eq), .in3(comparator_8_eq), .in4(or_2_out),
    .in5(comparator_11_eq), .in7(comparator_12_eq), .out(format));  // open: in6, en_in, gs, en_out

  // Notes on the sheet:
  //   R
  //   I
  //   S
  //   B
  //   U
  //   J
  //   0
endmodule
